# Fritzing sketch CircuitoMiniBombaDeAgua (saved by Fritzing 0.9.4)
breadboards: 1

parts:
  Componente1 = Arduino Uno (Rev3) - ICSP
  X3 = USB Connectors [package=usb-a-s-nosilk]
  X4 = USB Connectors [package=usb-a-pcb]  # not connected
  U1 = 4-Channel 5v Relay Shield [package=relay-4ch5v10a]
  M2 = DC Motor

nets:
  N1: Componente1.D9_PWM, U1.IN2
  5V: Componente1.5V, U1.VCC
  GND: Componente1.GND, U1.GND
  N2: X3.D+, M2.pin_2
  N3: X3.D-, U1.K2-Off
  N4: U1.K2-On, M2.pin_1

notes:
  Entrada USB Powerbank/Fuente
  Voltaje Máximo  5vc
  Mini Bomba de Agua
  Módulo 4 Relés
  CircuitoMiniBombaDeAgua
  Andrés Weitzel
  Estado Normal
  OpenSource2021
  Diseñado en fritzing
  Abierto (IN2)

custom parts:
  4-Channel 5v Relay Shield: 4 Channel 5v Relay Shield w. 2x SPD-06VDC-SD-C
