# Fritzing sketch CircuitoControlSensoresDeAgua (saved by Fritzing 0.9.4)
breadboards: 1

parts:
  Componente3 = Arduino Uno (Rev3) - ICSP
  U3 = 4-Channel 5v Relay Shield [package=relay-4ch5v10a]
  X6 = USB Connectors [package=usb-a-s-nosilk]  # not connected
  Sensor_de_Agua3 = Water Level Sensor
  YL-83_-_Detection_Board2 = YL-83 Rain Sensor - Detection Board
  YL-83_-_Control_Board2 = YL-83 Rain Sensor - Control Board
  LED1 = smd LED [color="Blue (470nm)" package="0603 [SMD]"]
  LED2 = smd LED [color="Red (635nm)" package="0603 [SMD]"]
  R1 = Resistor [tolerance=±5% resistance=220 package="2010 [SMD]"]
  R2 = Resistor [tolerance=±5% resistance=220 package="2010 [SMD]"]
  S6 = Piezo-electric buzzer

nets:
  N1: Componente3.A0, Sensor_de_Agua3.SIG
  N2: Componente3.A1, YL-83_-_Control_Board2.AO
  N3: Componente3.D13/SCK, U3.IN4
  N4: Componente3.D2, LED1.anode
  N5: Componente3.D3_PWM, LED2.anode
  N6: Componente3.D4, S6.Signal
  VCC: Componente3.5V, U3.VCC, U3.K4-Off, S6.Vcc
  GND: Componente3.GND, U3.GND, Sensor_de_Agua3.GND, YL-83_-_Control_Board2.GND, R1.Pin_0, R2.Pin_0, S6.Gnd
  N7: U3.K4-On, Sensor_de_Agua3.VCC
  N8: YL-83_-_Detection_Board2.POS, YL-83_-_Control_Board2.POS
  N9: YL-83_-_Detection_Board2.NEG, YL-83_-_Control_Board2.NEG
  N10: LED1.cathode, R1.Pin_1
  N11: LED2.cathode, R2.Pin_1

notes:
  Entrada USB Powerbank/Fuente
  Sensor de Agua MH 5vc
  Circuito Control Sensores de Agua
  Andrés Weitzel
  Diseñado en fritzing
  OpenSource2021
  Módulo 4 Relés
  Estado Normal Abierto (IN4)
  Módulo Controlador
  Módulo Sensor
  Sensor de Agua MH-RD 5vc
  Circuito Sensor De Agua MH-RD
  Estado Normal Abierto
  (Ambos Sensores Conectados
  nos ahorramos 1 relé)
  Leds Y Resistores
  Modulo Buzzer
  Activo MH-FMD

custom parts:
  4-Channel 5v Relay Shield: 4 Channel 5v Relay Shield w. 2x SPD-06VDC-SD-C
  Water Level Sensor: A water level sensor. This sensor operates at 3V to 5V. The Sig (signal) pin outputs an analogue signal that is in proportion to the amount of water in contact with the sensor.
  YL-83 Rain Sensor - Detection Board: The YL-83 is a rain sensor that has more resistance when dry and less resistance when wet. The module runs at 5V.
  YL-83 Rain Sensor - Control Board: The YL-83 is a rain sensor that has more resistance when dry and less resistance when wet. The module runs at 5V.
  Piezo-electric buzzer: Piezo-electric buzzer (speaker)
