# Fritzing sketch CircuitoSensorDeAguaMH (saved by Fritzing 0.9.4)
breadboards: 1

parts:
  Componente2 = Arduino Uno (Rev3) - ICSP
  Sensor_de_Agua2 = Water Level Sensor
  X5 = USB Connectors [package=usb-a-s-nosilk]  # not connected
  U2 = 4-Channel 5v Relay Shield [package=relay-4ch5v10a]

nets:
  N1: Componente2.A0, Sensor_de_Agua2.SIG
  N2: Componente2.D12/MISO, U2.IN4
  5V: Componente2.5V, U2.VCC
  GND: Componente2.GND, Sensor_de_Agua2.GND, U2.GND, U2.K4-Off
  N3: Sensor_de_Agua2.VCC, U2.K4-On

notes:
  Sensor de Agua MH 5vc
  Circuito Sensor De Agua MH
  Andrés Weitzel
  OpenSource2021
  Entrada USB Powerbank/Fuente
  Diseñado en fritzing
  Estado Normal
  Módulo 4 Relés
  Abierto (IN4)
  (Produce varios cambios de estados en intervalos pequeños)
  Pin13 NO recomendado para rele

custom parts:
  Water Level Sensor: A water level sensor. This sensor operates at 3V to 5V. The Sig (signal) pin outputs an analogue signal that is in proportion to the amount of water in contact with the sensor.
  4-Channel 5v Relay Shield: 4 Channel 5v Relay Shield w. 2x SPD-06VDC-SD-C
