# Fritzing sketch CircuitoSensorDeAguaMH_RD (saved by Fritzing 0.9.4)
breadboards: 1

parts:
  YL-83_-_Detection_Board1 = YL-83 Rain Sensor - Detection Board
  YL-83_-_Control_Board1 = YL-83 Rain Sensor - Control Board
  Componente3 = Arduino Uno (Rev3) - ICSP
  X6 = USB Connectors [package=usb-a-s-nosilk]  # not connected
  U3 = 4-Channel 5v Relay Shield [package=relay-4ch5v10a]

nets:
  N1: YL-83_-_Detection_Board1.POS, YL-83_-_Control_Board1.POS
  N2: YL-83_-_Detection_Board1.NEG, YL-83_-_Control_Board1.NEG
  N3: YL-83_-_Control_Board1.VCC, U3.K4-On
  GND: YL-83_-_Control_Board1.GND, Componente3.GND, U3.GND
  N4: YL-83_-_Control_Board1.AO, Componente3.A1
  N5: Componente3.D12/MISO, U3.IN4
  5V: Componente3.5V, U3.VCC, U3.K4-Off

notes:
  Entrada USB Powerbank/Fuente
  Sensor de Agua MH-RD 5vc
  Módulo Sensor
  Módulo Controlador
  Andrés Weitzel
  Diseñado en fritzing
  OpenSource2021
  Circuito Sensor De Agua MH-RD
  Estado Normal
  Módulo 4 Relés
  Abierto (IN4)
  Pin13 NO recomendado para rele
  (Produce varios cambios de estados en intervalos pequeños)

custom parts:
  YL-83 Rain Sensor - Detection Board: The YL-83 is a rain sensor that has more resistance when dry and less resistance when wet. The module runs at 5V.
  YL-83 Rain Sensor - Control Board: The YL-83 is a rain sensor that has more resistance when dry and less resistance when wet. The module runs at 5V.
  4-Channel 5v Relay Shield: 4 Channel 5v Relay Shield w. 2x SPD-06VDC-SD-C
