# Fritzing sketch CircuitoSistemaDeRiegoAutomatico (saved by Fritzing 0.9.4)
breadboards: 1

parts:
  Componente2 = Arduino Uno (Rev3) - ICSP
  X5 = USB Connectors [package=usb-a-pcb]  # not connected
  X6 = USB Connectors [package=usb-a-s-nosilk]
  KY-3 = Keyes Relay [package=THT]
  M3 = DC Motor
  Sensor_de_Agua1 = Water Level Sensor  # not connected

nets:
  N1: Componente2.D13/SCK, KY-3.signal
  N2: Componente2.GND, KY-3.ground
  N3: X6.D+, M3.pin_2
  N4: X6.D-, KY-3.C
  N5: KY-3.NO, M3.pin_1

notes:
  Entrada USB Powerbank
  Voltaje Máximo de Salida 5vc
  Bomba de Agua
  Estado Normal Abierto
  Relé
  CircuitoSistemaDeRiegoAutomático
  OpenSource2021
  Andrés Weitzel
  Sensor de Agua

custom parts:
  Keyes Relay: The Keyes 5V relay module is suitable for SCM development, home appliance control. It uses a 5V~12V TIL control signal which can control DC / AC signal.
  Water Level Sensor: A water level sensor. This sensor operates at 3V to 5V. The Sig (signal) pin outputs an analogue signal that is in proportion to the amount of water in contact with the sensor.
